// Logisim project Laboratorio2.circ as structural Verilog: 2 circuits, main circuit main
module main (
  input  [3:0] in_1
);

  wire a, b, c, d, e, f, g;

  BCD7SEG bcd7seg_1 (
    .w(in_1[3]), .x(in_1[2]), .y(in_1[1]), .z(in_1[0]), .a(a), .b(b), .c(c), .d(d), .e(e), .f(f), .g(g));
  _7_Segment_Display u_7_segment_display_1 (.g(g), .f(f), .a(a), .b(b), .e(e), .d(d), .c(c));  // open: dp
endmodule

module BCD7SEG (
  input  w,
  input  x,
  input  y,
  input  z,
  output a,
  output b,
  output c,
  output d,
  output e,
  output f,
  output g
);

  wire and_1_out, and_2_out, and_3_out, and_4_out, and_5_out, and_6_out, and_7_out, and_8_out, and_9_out,
       and_10_out, and_11_out, and_12_out, and_13_out, and_14_out, and_15_out, and_16_out, and_17_out,
       and_18_out, and_19_out, and_20_out, and_21_out, and_22_out, and_23_out, and_24_out, and_25_out,
       not_1_out, not_2_out, not_3_out, not_4_out;

  not not_1 (not_1_out, w);
  not not_2 (not_2_out, x);
  not not_3 (not_3_out, y);
  not not_4 (not_4_out, z);
  and and_1 (and_1_out, not_1_out, not_2_out, not_4_out);
  and and_2 (and_2_out, not_1_out, y);
  and and_3 (and_3_out, not_1_out, x, z);
  and and_4 (and_4_out, w, not_2_out, not_3_out);
  and and_5 (and_5_out, not_1_out, not_2_out);
  and and_6 (and_6_out, not_1_out, not_3_out, not_4_out);
  and and_7 (and_7_out, not_2_out, not_3_out);
  and and_8 (and_8_out, not_1_out, y, z);
  and and_9 (and_9_out, not_2_out, not_3_out);
  and and_10 (and_10_out, not_1_out, z);
  and and_11 (and_11_out, not_1_out, x);
  and and_12 (and_12_out, not_2_out, not_3_out, not_4_out);
  and and_13 (and_13_out, not_1_out, not_2_out, y);
  and and_14 (and_14_out, not_1_out, y, not_4_out);
  and and_15 (and_15_out, not_1_out, x, not_3_out, z);
  and and_16 (and_16_out, not_2_out, not_3_out, not_4_out);
  and and_17 (and_17_out, not_1_out, y, not_4_out);
  and and_18 (and_18_out, not_1_out, not_3_out, not_4_out);
  and and_19 (and_19_out, not_1_out, x, not_3_out);
  and and_20 (and_20_out, not_1_out, x, not_4_out);
  and and_21 (and_21_out, w, not_2_out, not_3_out);
  and and_22 (and_22_out, not_1_out, not_2_out, y);
  and and_23 (and_23_out, not_1_out, x, not_3_out);
  and and_24 (and_24_out, not_1_out, x, not_4_out);
  and and_25 (and_25_out, w, not_2_out, not_3_out);
  or or_1 (a, and_1_out, and_2_out, and_3_out, and_4_out);
  or or_2 (b, and_5_out, and_6_out, and_7_out, and_8_out);
  or or_3 (c, and_9_out, and_10_out, and_11_out);
  or or_4 (d, and_12_out, and_13_out, and_14_out, and_15_out);
  or or_5 (e, and_16_out, and_17_out);
  or or_6 (f, and_18_out, and_19_out, and_20_out, and_21_out);
  or or_7 (g, and_22_out, and_23_out, and_24_out, and_25_out);
endmodule
